// Logisim project TEMPT.circ as structural Verilog
module ALU_Control (
  input  OP5,
  input  OP4,
  input  OP3,
  input  OP2,
  input  OP1,
  input  OP0,
  input  FUNC5,
  input  FUNC4,
  input  FUNC3,
  input  FUNC2,
  input  FUNC1,
  input  FUNC0,
  output ALUOP3,
  output ALUOP2,
  output ALUOP1,
  output ALUOP0,
  output ChooseALU1,
  output ChooseALU2,
  output ChooseALU3,
  output ShiftLocat
);

  wire and_2_out, and_3_out, and_4_out, and_5_out, and_6_out, and_7_out, and_8_out, and_9_out, and_10_out,
       and_11_out, not_1_out, not_2_out, not_3_out, not_4_out, not_5_out, not_6_out, not_7_out, not_8_out,
       not_9_out, not_10_out, not_11_out, not_12_out, not_13_out, not_14_out, not_15_out;

  not not_1 (not_1_out, OP0);
  not not_2 (not_2_out, FUNC5);
  not not_3 (not_3_out, FUNC3);
  not not_4 (not_4_out, FUNC0);
  not not_5 (not_5_out, OP3);
  not not_6 (not_6_out, OP1);
  not not_7 (not_7_out, OP3);
  and and_1 (ALUOP2, not_7_out, FUNC1);
  and and_2 (and_2_out, FUNC5, FUNC0);
  not not_8 (not_8_out, OP3);
  not not_9 (not_9_out, FUNC5);
  and and_3 (and_3_out, not_8_out, not_9_out, FUNC0);
  not not_10 (not_10_out, OP3);
  not not_11 (not_11_out, FUNC5);
  not not_12 (not_12_out, OP3);
  not not_13 (not_13_out, FUNC5);
  and and_4 (and_4_out, not_12_out, not_13_out, FUNC3);
  and and_5 (and_5_out, OP2, OP1, OP0);
  not not_14 (not_14_out, OP3);
  and and_6 (and_6_out, not_14_out, FUNC3);
  not not_15 (not_15_out, OP2);
  and and_7 (and_7_out, not_15_out, OP1);
  not not_16 (ShiftLocat, FUNC2);
  and and_8 (and_8_out, not_1_out, not_2_out, FUNC4, not_3_out, FUNC2, FUNC1, not_4_out);
  and and_9 (and_9_out, not_5_out, FUNC5, FUNC2);
  and and_10 (and_10_out, OP2, not_6_out);
  and and_11 (and_11_out, OP2, OP0);
  or or_1 (ALUOP1, and_2_out, OP0, OP1);
  or or_2 (ALUOP0, and_3_out, OP1);
  and and_12 (ChooseALU1, not_10_out, not_11_out, FUNC3, FUNC0);
  or or_3 (ChooseALU2, and_4_out, and_5_out);
  or or_4 (ChooseALU3, and_6_out, and_7_out);
  or or_5 (ALUOP3, and_8_out, and_9_out, and_10_out, and_11_out);
endmodule

module SLT (
  input  [4:0] Rs,
  input  [4:0] Rt,
  output SLTReturn
);

  Comparator #(.width(5)) comparator_1 (.a(Rs), .b(Rt), .lt(SLTReturn));  // open: gt, eq
endmodule
